# Fritzing sketch all pins (saved by Fritzing 0.9.3b)
breadboards: 1

parts:
  Part1 =  Arduino-Zero
  J1 = Basic Servo
  K3 = Relay [part_number=FRS1B-S package=THT]
  LM1 = RioRand LM2596
  LM2 = RioRand LM2596
  J2 = Basic Servo
  J3 = Basic Servo
  J4 = Basic Servo
  J5 = Basic Servo
  Power_plug1 = Power plug
  Q4 = NPN-Transistor [package="SOT-23 [SMD]"]
  R1 = Resistor [tolerance=±5% resistance=1k package=THT]
  D5 = Rectifier Diode [part_number=1N4001 package="300 mil [THT]"]

nets (from the breadboard view):
  N1: Part1.connector5, R1.Pin_0
  N2: Part1.connector86, K3.COIL2, D5.cathode
  N3: Part1.connector88, Power_plug1.GND, Q4.2
  N4: Part1.connector90, K3.C1, K3.C2, Power_plug1.VCC
  GND: J1.gnd, LM1.Pin_3, J2.gnd, J3.gnd
  VCC: J1.vcc, LM1.Pin_2, J2.vcc, J3.vcc
  N5: K3.COIL1, Q4.1, D5.anode
  VCC_2: LM2.Pin_2, J4.vcc, J5.vcc
  GND_2: LM2.Pin_3, J4.gnd, J5.gnd
  N6: Q4.0, R1.Pin_1

notes:
  12v 5A power supply -->>
  12v
  7.4v
  6v
  pin A5 LOW to turn off servos, HIGH to turn on
  HS-422
  HS-645MG
  HS-8775MG
  HS-8335SH
  HS-8330SH
  servo PWMs
  5 base;
  6 shoulder
  9 elbow;
  10 wrist;
  11 gripper
  2x LED matrix
  2 clk;
  3 CS;
  4 DIN
  -> shift register board
  7 CE;
  8 PL;
  12 CP;
  13 output
  random seed generating analogRead(0)
  update to reflect a ctual
  BC547B transistor has collector and emitter other way around (has to be swapped from diagram)!
