# Fritzing sketch servo power 2 (saved by Fritzing 0.9.3b)
breadboards: 1

parts:
  J1 = Basic Servo
  K3 = Relay [part_number=FRS1B-S package=THT]
  D4 = Rectifier Diode [part_number=1N4001 package="300 mil [THT]"]
  R5 = Resistor [resistance=1k tolerance=±5% package=THT]
  LM1 = RioRand LM2596
  LM2 = RioRand LM2596
  J2 = Basic Servo
  J3 = Basic Servo
  J4 = Basic Servo
  J5 = Basic Servo
  Q4 = NPN-Transistor [package="SOT-23 [SMD]"]
  Power_plug1 = Power plug
  Part2 = Arduino Due (Rev2b)

nets:
  GND: J1.gnd, LM1.Pin_3, J2.gnd, J3.gnd
  VCC: J1.vcc, LM1.Pin_2, J2.vcc, J3.vcc
  N1: K3.COIL1, D4.anode, Q4.1
  VCC_2: K3.C1, K3.C2, Power_plug1.VCC, Part2.VIN
  N2: K3.COIL2, D4.cathode, Part2.IOREF
  N3: R5.Pin_0, Q4.0
  N4: R5.Pin_1, Part2.D9_PWM
  VCC_3: LM2.Pin_2, J4.vcc, J5.vcc
  GND_2: LM2.Pin_3, J4.gnd, J5.gnd
  N5: Q4.2, Part2.GND

notes:
  12v 5A power supply -->>
  12v
  7.4v
  6v
  pin 9 LOW to turn off servos, HIGH to turn on
  HS-422
  HS-645MG
  HS-8775MG
  HS-8335SH
  HS-8330SH
