# Fritzing sketch shift register circuit 3(no led) (saved by Fritzing 0.9.3b)
breadboards: 4

parts:
  R4 = Resistor [tolerance=±5% resistance=1k package=THT]
  R5 = Resistor [tolerance=±5% resistance=1k package=THT]
  R7 = Resistor [tolerance=±5% resistance=1k package=THT]
  R10 = Resistor [tolerance=±5% resistance=1k package=THT]
  R11 = Resistor [tolerance=±5% resistance=1k package=THT]
  R12 = Resistor [tolerance=±5% resistance=1k package=THT]
  R13 = Resistor [tolerance=±5% resistance=1k package=THT]
  R14 = Resistor [tolerance=±5% resistance=1k package=THT]
  R15 = Resistor [tolerance=±5% resistance=1k package=THT]
  R16 = Resistor [tolerance=±5% resistance=1k package=THT]
  R19 = Resistor [tolerance=±5% resistance=1k package=THT]
  R20 = Resistor [tolerance=±5% resistance=1k package=THT]
  R21 = Resistor [tolerance=±5% resistance=1k package=THT]
  R22 = Resistor [tolerance=±5% resistance=1k package=THT]
  U18 = 74HC165 [part_number=SN74LS165 package="DIP16 [THT]"]
  U19 = 74HC165 [part_number=SN74LS165 package="DIP16 [THT]"]
  U20 = 74HC165 [part_number=SN74LS165 package="DIP16 [THT]"]
  U21 = 74HC165 [part_number=SN74LS165 package="DIP16 [THT]"]
  U24 = 74HC165 [part_number=SN74LS165 package="DIP16 [THT]"]
  R23 = Resistor [tolerance=±5% resistance=1k package=THT]
  R24 = Resistor [tolerance=±5% resistance=1k package=THT]
  R25 = Resistor [tolerance=±5% resistance=1k package=THT]
  R26 = Resistor [tolerance=±5% resistance=1k package=THT]
  R27 = Resistor [tolerance=±5% resistance=1k package=THT]
  R28 = Resistor [tolerance=±5% resistance=1k package=THT]
  R29 = Resistor [tolerance=±5% resistance=1k package=THT]
  R30 = Resistor [tolerance=±5% resistance=1k package=THT]
  R31 = Resistor [tolerance=±5% resistance=1k package=THT]
  R32 = Resistor [tolerance=±5% resistance=1k package=THT]
  R33 = Resistor [tolerance=±5% resistance=1k package=THT]
  R34 = Resistor [tolerance=±5% resistance=1k package=THT]
  C1 = Ceramic Capacitor [capacitance=0.1µF package="100 mil [THT, multilayer]"]
  C2 = Ceramic Capacitor [capacitance=0.1µF package="100 mil [THT, multilayer]"]
  C3 = Ceramic Capacitor [capacitance=0.1µF package="100 mil [THT, multilayer]"]
  C4 = Ceramic Capacitor [capacitance=0.1µF package="100 mil [THT, multilayer]"]
  R35 = Resistor [tolerance=±5% resistance=1k package=THT]
  R36 = Resistor [tolerance=±5% resistance=1k package=THT]
  R37 = Resistor [tolerance=±5% resistance=1k package=THT]
  R38 = Resistor [tolerance=±5% resistance=1k package=THT]
  R39 = Resistor [tolerance=±5% resistance=1k package=THT]
  R40 = Resistor [tolerance=±5% resistance=1k package=THT]
  R41 = Resistor [tolerance=±5% resistance=1k package=THT]
  R42 = Resistor [tolerance=±5% resistance=1k package=THT]
  R43 = Resistor [tolerance=±5% resistance=1k package=THT]
  R44 = Resistor [tolerance=±5% resistance=1k package=THT]
  R45 = Resistor [tolerance=±5% resistance=1k package=THT]
  R46 = Resistor [tolerance=±5% resistance=1k package=THT]
  R47 = Resistor [tolerance=±5% resistance=1k package=THT]
  R48 = Resistor [tolerance=±5% resistance=1k package=THT]
  R49 = Resistor [tolerance=±5% resistance=1k package=THT]
  R50 = Resistor [tolerance=±5% resistance=1k package=THT]
  R51 = Resistor [tolerance=±5% resistance=1k package=THT]
  R52 = Resistor [tolerance=±5% resistance=1k package=THT]
  R53 = Resistor [tolerance=±5% resistance=1k package=THT]
  R54 = Resistor [tolerance=±5% resistance=1k package=THT]
  R55 = Resistor [tolerance=±5% resistance=1k package=THT]
  R56 = Resistor [tolerance=±5% resistance=1k package=THT]
  C5 = Ceramic Capacitor [capacitance=0.1µF package="100 mil [THT, multilayer]"]
  R57 = Resistor [tolerance=±5% resistance=220 package=THT]
  R59 = Resistor [tolerance=±5% resistance=1k package=THT]
  R60 = Resistor [tolerance=±5% resistance=1k package=THT]
  R61 = Resistor [tolerance=±5% resistance=1k package=THT]
  Part1 = Arduino Due (Rev2b)
  C7 = Tantalum Capacitor [capacitance=1μF package="100 mil [THT, tantalum]"]
  U27 = 74HC165 [part_number=SN74LS165 package="DIP16 [THT]"]
  C8 = Ceramic Capacitor [capacitance=0.1µF package="100 mil [THT, multilayer]"]
  R62 = Resistor [tolerance=±5% resistance=220 package=THT]
  R63 = Resistor [tolerance=±5% resistance=1k package=THT]
  R64 = Resistor [tolerance=±5% resistance=1k package=THT]
  R65 = Resistor [tolerance=±5% resistance=1k package=THT]
  U28 = 74HC165 [part_number=SN74LS165 package="DIP16 [THT]"]
  C9 = Ceramic Capacitor [capacitance=0.1µF package="100 mil [THT, multilayer]"]
  R66 = Resistor [tolerance=±5% resistance=220 package=THT]
  R67 = Resistor [tolerance=±5% resistance=1k package=THT]
  R68 = Resistor [tolerance=±5% resistance=1k package=THT]
  R69 = Resistor [tolerance=±5% resistance=1k package=THT]
  U29 = 74HC165 [part_number=SN74LS165 package="DIP16 [THT]"]
  C10 = Ceramic Capacitor [capacitance=0.1µF package="100 mil [THT, multilayer]"]
  R70 = Resistor [tolerance=±5% resistance=220 package=THT]
  R71 = Resistor [tolerance=±5% resistance=1k package=THT]
  R72 = Resistor [tolerance=±5% resistance=1k package=THT]
  R73 = Resistor [tolerance=±5% resistance=1k package=THT]

nets:
  GND: R4.Pin_0, R5.Pin_0, R7.Pin_0, R10.Pin_0, R11.Pin_0, R12.Pin_0, R13.Pin_0, R14.Pin_0, R15.Pin_0, R16.Pin_0, R19.Pin_1, R20.Pin_1, R21.Pin_1, R22.Pin_1, U18.GND, U19.GND, U21.GND, R27.Pin_1, R28.Pin_1, R29.Pin_1, R30.Pin_1, R31.Pin_1, R32.Pin_1, R33.Pin_1, R34.Pin_1, C1.0, C2.0, C3.0, C4.0, R51.Pin_0, R52.Pin_0, R53.Pin_0, R54.Pin_0, R55.Pin_0, R56.Pin_0
  N1: R4.Pin_1, U18.D7
  N2: R5.Pin_1, U18.D6
  N3: R7.Pin_1, U19.D5
  N4: R10.Pin_1, U19.D4
  N5: R11.Pin_1, U20.D5
  N6: R12.Pin_1, U20.D4
  N7: R13.Pin_1, U20.D7
  N8: R14.Pin_1, U20.D6
  N9: R15.Pin_1, U21.D7
  N10: R16.Pin_1, U21.D6
  N11: R19.Pin_0, U21.D3
  N12: R20.Pin_0, U21.D2
  N13: R21.Pin_0, U21.D1
  N14: R22.Pin_0, U21.D0
  N15: U18.D0, R31.Pin_0
  N16: U18.D1, R32.Pin_0
  N17: U18.D2, R33.Pin_0
  N18: U18.D3, R34.Pin_0
  N19: U18.D4, R51.Pin_1
  N20: U18.D5, R52.Pin_1
  N21: U18.PL, U19.PL, U20.PL, U21.PL, U24.PL, Part1.D22, U27.PL, U28.PL, U29.PL
  N22: U18.CP, U19.CP, U20.CP, U21.CP
  N23: U18.CE, U19.CE, U21.CE, U24.CE, Part1.D24, U27.CE, U28.CE, U29.CE
  N24: U18.Q7, Part1.D28
  N25: U18.DS, U19.Q7
  VCC: U18.VCC, U19.VCC, U20.VCC, U21.VCC, U24.VCC, C1.1, C2.1, C3.1, C4.1, C5.1, Part1.IOREF, C7.-, U27.VCC, C8.1, U28.VCC, C9.1, U29.VCC, C10.1
  N26: U19.D0, R27.Pin_0
  N27: U19.D1, R28.Pin_0
  N28: U19.D2, R29.Pin_0
  N29: U19.D3, R30.Pin_0
  N30: U19.D6, R53.Pin_1
  N31: U19.D7, R54.Pin_1
  N32: U19.DS, U20.Q7
  N33: U20.D0, R23.Pin_0
  N34: U20.D1, R24.Pin_0
  N35: U20.D2, R25.Pin_0
  N36: U20.D3, R26.Pin_0
  N37: U20.GND, R23.Pin_1, R24.Pin_1, R25.Pin_1, R26.Pin_1
  N38: U20.DS, U21.Q7
  N39: U21.D4, R56.Pin_1
  N40: U21.D5, R55.Pin_1
  N41: U21.DS, U24.Q7
  N42: U24.D0, R35.Pin_0
  N43: U24.D1, R36.Pin_0
  N44: U24.D2, R38.Pin_0
  N45: U24.D3, R37.Pin_0
  N46: U24.D4, R60.Pin_0
  N47: U24.D5, R59.Pin_0
  N48: U24.D6, R61.Pin_0
  GND_2: U24.GND, R35.Pin_1, R36.Pin_1, R37.Pin_1, R38.Pin_1, R39.Pin_1, R40.Pin_1, R41.Pin_1, R42.Pin_1, R43.Pin_1, R44.Pin_1, R45.Pin_1, R46.Pin_1, R47.Pin_1, R48.Pin_1, R49.Pin_1, R50.Pin_1, C5.0, R57.Pin_0, R59.Pin_1, R60.Pin_1, R61.Pin_1, Part1.GND, C7.+, C8.0, R62.Pin_0, U28.GND, R66.Pin_0, R67.Pin_1, R68.Pin_1, R69.Pin_1, U29.GND, C10.0, R70.Pin_0, R71.Pin_1, R72.Pin_1, R73.Pin_1
  N49: U24.CP, Part1.D26, U28.CP, U29.CP
  N50: U24.D7, R57.Pin_1
  N51: U24.DS, U27.Q7
  N52: R39.Pin_0, U27.D1
  N53: R40.Pin_0, U27.D0
  N54: R41.Pin_0, U27.D3
  N55: R42.Pin_0, U27.D2
  N56: R43.Pin_0, U28.D3
  N57: R44.Pin_0, U28.D2
  N58: R45.Pin_0, U28.D1
  N59: R46.Pin_0, U28.D0
  N60: R47.Pin_0, U29.D3
  N61: R48.Pin_0, U29.D0
  N62: R49.Pin_0, U29.D1
  N63: R50.Pin_0, U29.D2
  N64: U27.D4, R64.Pin_0
  N65: U27.D5, R65.Pin_0
  N66: U27.D6, R63.Pin_0
  N67: U27.GND, R63.Pin_1, R64.Pin_1, R65.Pin_1
  N68: U27.D7, R62.Pin_1
  N69: U27.DS, U28.Q7
  N70: U28.D4, R68.Pin_0
  N71: U28.D5, R69.Pin_0
  N72: U28.D6, R67.Pin_0
  N73: U28.D7, R66.Pin_1
  N74: U28.DS, U29.Q7
  N75: U29.D4, R72.Pin_0
  N76: U29.D5, R73.Pin_0
  N77: U29.D6, R71.Pin_0
  N78: U29.D7, R70.Pin_1

notes:
  CP
  Vcc CE
  PL GND
  CP PL GND
  Vcc GND
  Cap B
  Caps C1-8
  inputs
  1-8
  inputs
  9-16
  inputs
  17-24
  inputs
  25-32
  inputs
  57-64
  inputs
  41-48
  inputs
  33-40
  inputs
  49-56

custom parts:
  74HC165: 8-bit parallel-load shift registers
